// Logisim project alu.circ as structural Verilog: 13 circuits, main circuit main
module main (
  input  [15:0] X,
  input  [15:0] Y,
  input  [3:0] Switch__S,
  output Signed_Overflow,
  output [15:0] RESULT,
  output Equal
);

  wire addp8s, addp8u, adds, addu, and_3_out, and_4_out, and_6_out, and_7_out, comparator_1_eq,
       comparator_2_eq, comparator_3_eq, comparator_4_eq, subp8s, subs;
  wire [15:0] add_out, addp8_out, and_out, or_out, sllv_out, slt_out, srav_out, srlv_out, sub_out, subp8_out;

  add add (.Input1(X), .Input2(Y), .out(add_out), .out_2(addu), .out_3(adds));
  sub sub (.Input1(X), .Input2(Y), .out(sub_out), .out_2(subs));
  sllv sllv (.Input1(X), .Input2(Y), .out(sllv_out));
  srlv srlv (.Input1(X), .Input2(Y), .out(srlv_out));
  srav srav (.Input1(X), .Input2(Y), .out(srav_out));
  slt slt (.Input1(X), .Input2(Y), .out(slt_out));
  \or  \or  (.Input1(X), .Input2(Y), .out(or_out));
  \and  \and  (.Input1(X), .Input2(Y), .out(and_out));
  addp8 addp8 (.Input1(X), .Input2(Y), .out(addp8_out), .out_2(addp8u), .out_3(addp8s));
  subp8 subp8 (.Input1(X), .Input2(Y), .out(subp8_out), .out_2(subp8s));
  Multiplexer #(.select(4), .width(16), .enable("false")) multiplexer_1 (
    .in0(add_out), .in1(sub_out), .in2(sllv_out), .in3(srlv_out), .in4(srav_out), .in5(slt_out),
    .in6(or_out), .in7(and_out), .in8(addp8_out), .in9(subp8_out), .out(RESULT), .sel(Switch__S));  // open: in10, in11, in12, in13, in14, in15
  Comparator #(.width(4)) comparator_1 (.a(Switch__S), .b(4'b0000), .eq(comparator_1_eq));  // open: gt, lt
  Comparator #(.width(4)) comparator_2 (.a(Switch__S), .b(4'b0001), .eq(comparator_2_eq));  // open: gt, lt
  Comparator #(.width(4)) comparator_3 (.a(Switch__S), .b(4'b1000), .eq(comparator_3_eq));  // open: gt, lt
  Comparator #(.width(4)) comparator_4 (.a(Switch__S), .b(4'b1001), .eq(comparator_4_eq));  // open: gt, lt
  Comparator #(.width(16)) comparator_5 (.a(X), .b(Y), .eq(Equal));  // open: gt, lt
  // AND_Gate and_2 has open pins: in0=addu, in1=comparator_1_eq, out=open
  and and_3 (and_3_out, comparator_1_eq, adds);
  and and_4 (and_4_out, comparator_2_eq, subs);
  // AND_Gate and_5 has open pins: in0=addp8u, in1=comparator_3_eq, out=open
  and and_6 (and_6_out, comparator_3_eq, addp8s);
  and and_7 (and_7_out, comparator_4_eq, subp8s);
  or or_2 (Signed_Overflow, and_3_out, and_4_out, and_6_out, and_7_out);

  // Notes on the sheet:
  //   INPUTS to your circuit
  //   INPUT to your circuit
  //   DON'T CHANGE THE INPUTS AND OUTPUTS! IF YOU DO SO, YOU NEED TO MAKE SURE THE PINS ARE IN THE RIGHT PLACES!
  //   OUTPUTS of your circuit
endmodule

module add (
  input  [15:0] Input1,
  input  [15:0] Input2,
  output [15:0] out,
  output out_2,
  output out_3
);

  wire xnor_1_out, xor_1_out;

  Adder #(.width(16)) adder_1 (.a(Input1), .b(Input2), .out(out), .cout(out_2));  // open: cin
  xor xor_1 (xor_1_out, out[15], Input1[15]);
  and and_1 (out_3, xor_1_out, xnor_1_out);
  xnor xnor_1 (xnor_1_out, Input1[15], Input2[15]);
endmodule

module sub (
  input  [15:0] Input1,
  input  [15:0] Input2,
  output [15:0] out,
  output out_2
);

  wire xnor_1_out, xor_1_out;

  Subtractor #(.width(16)) subtractor_1 (.a(Input1), .b(Input2), .out(out));  // open: bin, bout
  xor xor_1 (xor_1_out, Input1[15], Input2[15]);
  xnor xnor_1 (xnor_1_out, out[15], Input2[15]);
  and and_1 (out_2, xor_1_out, xnor_1_out);
endmodule

module sllv (
  input  [15:0] Input1,
  input  [15:0] Input2,
  output [15:0] out
);

  wire [15:0] and_1_out;

  assign and_1_out = Input2 & 16'hf;  // AND_Gate and_1, 16 bits wide
  Shifter #(.width(16)) shifter_1 (.in(Input1), .\dist (and_1_out[3:0]), .out(out));
endmodule

module srlv (
  input  [15:0] Input1,
  input  [15:0] Input2,
  output [15:0] out
);

  wire [15:0] and_1_out;

  assign and_1_out = Input2 & 16'hf;  // AND_Gate and_1, 16 bits wide
  Shifter #(.width(16), .shift("lr")) shifter_1 (.in(Input1), .\dist (and_1_out[3:0]), .out(out));
endmodule

module srav (
  input  [15:0] Input1,
  input  [15:0] Input2,
  output [15:0] out
);

  wire [15:0] and_1_out;

  assign and_1_out = Input2 & 16'hf;  // AND_Gate and_1, 16 bits wide
  Shifter #(.width(16), .shift("ar")) shifter_1 (.in(Input1), .\dist (and_1_out[3:0]), .out(out));
endmodule

module slt (
  input  [15:0] Input1,
  input  [15:0] Input2,
  output [15:0] out
);

  Comparator #(.width(16)) comparator_1 (.a(Input1), .b(Input2), .lt(out[0]));  // open: gt, eq

  assign out[15:1] = {15{1'b0}};
endmodule

module \or  (
  input  [15:0] Input1,
  input  [15:0] Input2,
  output [15:0] out
);

  assign out = Input1 | Input2;  // OR_Gate or_1, 16 bits wide
endmodule

module \and  (
  input  [15:0] Input1,
  input  [15:0] Input2,
  output [15:0] out
);

  assign out = Input1 & Input2;  // AND_Gate and_1, 16 bits wide
endmodule

module addp8 (
  input  [15:0] Input1,
  input  [15:0] Input2,
  output [15:0] out,
  output out_2,
  output out_3
);

  wire adder8_1_out_2, adder8_1_out_3, adder8_2_out_2, adder8_2_out_3;

  adder8 adder8_1 (
    .Input1(Input1[7:0]), .Input2(Input2[7:0]), .out(out[7:0]), .out_2(adder8_1_out_2), .out_3(adder8_1_out_3));
  adder8 adder8_2 (
    .Input1(Input1[15:8]), .Input2(Input2[15:8]), .out(out[15:8]), .out_2(adder8_2_out_2),
    .out_3(adder8_2_out_3));
  or or_1 (out_2, adder8_1_out_2, adder8_2_out_2);
  or or_2 (out_3, adder8_1_out_3, adder8_2_out_3);
endmodule

module subp8 (
  input  [15:0] Input1,
  input  [15:0] Input2,
  output [15:0] out,
  output out_2
);

  wire sub8_1_out_2, sub8_2_out_2;

  sub8 sub8_1 (.Input1(Input1[7:0]), .Input2(Input2[7:0]), .out(out[7:0]), .out_2(sub8_1_out_2));
  sub8 sub8_2 (.Input1(Input1[15:8]), .Input2(Input2[15:8]), .out(out[15:8]), .out_2(sub8_2_out_2));
  or or_1 (out_2, sub8_1_out_2, sub8_2_out_2);
endmodule

module adder8 (
  input  [7:0] Input1,
  input  [7:0] Input2,
  output [7:0] out,
  output out_2,
  output out_3
);

  wire xnor_1_out, xor_1_out;

  Adder adder_1 (.a(Input1), .b(Input2), .out(out), .cout(out_2));  // open: cin
  xor xor_1 (xor_1_out, out[7], Input1[7]);
  and and_1 (out_3, xor_1_out, xnor_1_out);
  xnor xnor_1 (xnor_1_out, Input1[7], Input2[7]);
endmodule

module sub8 (
  input  [7:0] Input1,
  input  [7:0] Input2,
  output [7:0] out,
  output out_2
);

  wire xnor_1_out, xor_1_out;

  Subtractor subtractor_1 (.a(Input1), .b(Input2), .out(out));  // open: bin, bout
  xor xor_1 (xor_1_out, Input1[7], Input2[7]);
  xnor xnor_1 (xnor_1_out, out[7], Input2[7]);
  and and_1 (out_2, xor_1_out, xnor_1_out);
endmodule
